# Fritzing sketch schematic (saved by Fritzing 0.9.3b)
breadboards: 1

parts:
  Part1 = Arduino Mega ADK (Rev3)
  LED1 = smd LED [color="Red (633nm)" package="0805 [SMD]"]
  LED2 = smd LED [color="Red (633nm)" package="0805 [SMD]"]
  LED3 = smd LED [color="Red (633nm)" package="0805 [SMD]"]
  LED4 = smd LED [color="Red (633nm)" package="0805 [SMD]"]
  LED5 = smd LED [color="Red (633nm)" package="0805 [SMD]"]
  LED6 = smd LED [color="Red (633nm)" package="0805 [SMD]"]
  LED7 = smd LED [color="Red (633nm)" package="0805 [SMD]"]
  LED8 = smd LED [color="Red (633nm)" package="0805 [SMD]"]
  LED9 = smd LED [color="Red (633nm)" package="0805 [SMD]"]
  LED10 = smd LED [color="Red (633nm)" package="0805 [SMD]"]
  LED11 = smd LED [color="Red (633nm)" package="0805 [SMD]"]
  LED12 = smd LED [color="Red (633nm)" package="0805 [SMD]"]
  LED13 = smd LED [color="Red (633nm)" package="0805 [SMD]"]
  LED14 = smd LED [color="Red (633nm)" package="0805 [SMD]"]
  LED15 = smd LED [color="Red (633nm)" package="0805 [SMD]"]
  LED16 = smd LED [color="Red (633nm)" package="0805 [SMD]"]
  LED17 = smd LED [color="Red (633nm)" package="0805 [SMD]"]
  LED18 = smd LED [color="Red (633nm)" package="0805 [SMD]"]
  LED19 = smd LED [color="Red (633nm)" package="0805 [SMD]"]
  LED20 = smd LED [color="Red (633nm)" package="0805 [SMD]"]
  LED21 = smd LED [color="Red (633nm)" package="0805 [SMD]"]
  LED22 = smd LED [color="Red (633nm)" package="0805 [SMD]"]
  LED23 = smd LED [color="Red (633nm)" package="0805 [SMD]"]
  LED24 = smd LED [color="Red (633nm)" package="0805 [SMD]"]
  LED25 = smd LED [color="Red (633nm)" package="0805 [SMD]"]
  Matrix_keypad1 = KEYPAD 4x4

nets:
  N1: Part1.A0, Matrix_keypad1.row4
  N2: Part1.A1, Matrix_keypad1.row3
  N3: Part1.A2, Matrix_keypad1.row2
  N4: Part1.A3, Matrix_keypad1.row1
  N5: Part1.A4, Matrix_keypad1.col4
  N6: Part1.A5, Matrix_keypad1.col3
  N7: Part1.A6, Matrix_keypad1.col2
  N8: Part1.A7, Matrix_keypad1.col1
  N9: Part1.D21/SCL, LED20.anode
  N10: Part1.D20/SDA, LED19.anode
  N11: Part1.D19/RX1, LED18.anode
  N12: Part1.D18/TX1, LED17.anode
  N13: Part1.D17/RX2, LED16.anode
  N14: Part1.D16/TX2, LED15.anode
  N15: Part1.D15/RX3, LED14.anode
  N16: Part1.D14/TX3, LED13.anode
  N17: Part1.D13_PWM, LED12.anode
  N18: Part1.D12_PWM, LED11.anode
  N19: Part1.D11_PWM, LED10.anode
  N20: Part1.D10_PWM, LED9.anode
  N21: Part1.D9_PWM, LED8.anode
  N22: Part1.D8_PWM, LED7.anode
  N23: Part1.D2_PWM, LED1.anode
  N24: Part1.D3_PWM, LED2.anode
  N25: Part1.D4_PWM, LED3.anode
  N26: Part1.D5_PWM, LED4.anode
  N27: Part1.D6_PWM, LED5.anode
  N28: Part1.D7_PWM, LED6.anode
  N29: Part1.D22, LED21.anode
  N30: Part1.D23, LED22.anode
  N31: Part1.D24, LED23.anode
  N32: Part1.D25, LED24.anode
  N33: Part1.D26, LED25.anode
  GND: LED1.cathode, LED2.cathode, LED3.cathode, LED4.cathode, LED5.cathode, LED6.cathode, LED7.cathode, LED8.cathode, LED9.cathode, LED10.cathode, LED11.cathode, LED12.cathode, LED13.cathode, LED14.cathode, LED15.cathode, LED16.cathode, LED17.cathode, LED18.cathode, LED19.cathode, LED20.cathode, LED21.cathode, LED22.cathode, LED23.cathode, LED24.cathode, LED25.cathode

custom parts:
  KEYPAD 4x4: Matrix keypad 16 buttons, 4 rows x 4 columns
